// Logisim project D-FF using Latches.circ as structural Verilog: 1 circuit, main circuit main
module main (
  input  D,
  output Q
);

  wire CLK_out, multiplexer_1_out, not_1_out;

  Clock CLK (.out(CLK_out));
  Multiplexer multiplexer_1 (.in0(multiplexer_1_out), .in1(D), .out(multiplexer_1_out), .sel(CLK_out));
  Multiplexer multiplexer_2 (.in0(Q), .in1(multiplexer_1_out), .out(Q), .sel(not_1_out));
  not not_1 (not_1_out, CLK_out);
endmodule
