// Logisim project Synchronous UpDown Counter.circ as structural Verilog: 1 circuit, main circuit main
module main (
  input  x,
  output Q1,
  output Q0
);

  wire adder_1_out, adder_2_out, and_1_out, and_2_out, CLK_out, d_ff_1_qn, not_1_out, or_1_out;

  Clock CLK (.out(CLK_out));
  D_Flip_Flop d_ff_1 (.clk(CLK_out), .D(d_ff_1_qn), .Q(Q0), .Qn(d_ff_1_qn));  // open: preset, reset
  not not_1 (not_1_out, x);
  D_Flip_Flop d_ff_2 (.clk(CLK_out), .D(or_1_out), .Q(Q1));  // open: Qn, preset, reset
  Adder #(.width(1)) adder_1 (.a(Q1), .b(Q0), .out(adder_1_out));  // open: cin, cout
  Adder #(.width(1)) adder_2 (.a(d_ff_1_qn), .b(Q1), .out(adder_2_out));  // open: cin, cout
  and and_1 (and_1_out, adder_1_out, not_1_out);
  and and_2 (and_2_out, adder_2_out, x);
  or or_1 (or_1_out, and_1_out, and_2_out);
endmodule
