// Logisim project Latch using MUXs.circ as structural Verilog: 1 circuit, main circuit main
module main (
  input  Din,
  output R
);

  wire clock_1_out;

  Multiplexer multiplexer_1 (.in0(R), .in1(Din), .out(R), .sel(clock_1_out));
  Clock clock_1 (.out(clock_1_out));
endmodule
