// Logisim project MUX using Transmission gates.circ as structural Verilog: 1 circuit, main circuit main
module main (
  input  A,
  input  B,
  output R
);

  wire CLK_out, not_1_out;

  Clock CLK (.out(CLK_out));
  not not_1 (not_1_out, CLK_out);
  // Transmission_Gate transmission_1: pin names not known; wires that end beside it: A, CLK_out, not_1_out, R
  // Transmission_Gate transmission_2: pin names not known; wires that end beside it: B, not_1_out, CLK_out, R

  // Notes on the sheet:
  //   S'
endmodule
